# Fritzing sketch AUTO LIGHT (saved by Fritzing 0.9.3b)
breadboards: 1

parts:
  Часть1 = Arduino Uno (Rev3)
  LED1 = LED - 5mm [color="Red (633nm)" package="5 mm [THT]"]
  R1 = Resistor [tolerance=±5% resistance=220 package=THT]
  LED2 = LED - 5mm [color="Red (633nm)" package="5 mm [THT]"]
  R2 = Resistor [tolerance=±5% resistance=220 package=THT]
  S1 = Pushbutton [package="[THT]"]

nets:
  N1: Часть1.D3_PWM, R1.Pin_0
  N2: Часть1.D5_PWM, R2.Pin_1
  N3: LED1.cathode, LED2.cathode
  N4: LED1.anode, R1.Pin_1
  N5: LED2.anode, R2.Pin_0
  N6: S1.Pin_1, S1.Pin_2
  N7: S1.Pin_3, S1.Pin_4
