# Fritzing sketch PWM (saved by Fritzing 0.9.3b)
breadboards: 1

parts:
  Часть1 = Arduino Uno (Rev3)
  R1 = Resistor [tolerance=±5% resistance=220 package=THT]
  R2 = Resistor [tolerance=±5% resistance=220 package=THT]
  LED1 = LED - 5mm [color="Red (633nm)" package="5 mm [THT]"]
  R3 = Resistor [tolerance=±5% resistance=220 package=THT]
  LED2 = LED - 5mm [color="Red (633nm)" package="5 mm [THT]"]
  LED3 = LED - 5mm [color="Red (633nm)" package="5 mm [THT]"]  # not connected
  R4 = Resistor [tolerance=±5% resistance=220 package=THT]  # not connected
  LED4 = LED - 5mm [color="Red (633nm)" package="5 mm [THT]"]
  LED5 = LED - 5mm [color="Red (633nm)" package="5 mm [THT]"]
  R5 = Resistor [tolerance=±5% resistance=220 package=THT]
  X5 = Resistor [tolerance=±5% resistance=220 package=THT]  # not connected
  X5_2 = LED - 5mm [color="Red (633nm)" package="5 mm [THT]"]  # not connected

nets:
  N1: Часть1.D11_PWM/MOSI, R3.Pin_0, LED5.anode
  N2: Часть1.D5_PWM, R5.Pin_1
  N3: Часть1.D6_PWM, R1.Pin_0
  N4: Часть1.GND, LED2.cathode
  N5: R2.Pin_1, LED4.anode
  N6: LED1.anode, R3.Pin_1
